# Fritzing sketch head_arduino (saved by Fritzing 0.9.3b)

parts:
  Part1 = Arduino Mega 2560 (Rev3)
  S2 = Toggle Switch [package=THT]
  J1 = Dagu DGServo 9g header (male) [package=THT]
  J2 = Dagu DGServo 9g header (male) [package=THT]

nets:
  GND: Part1.GND, S2.L1, J1.gnd, J2.gnd
  N1: Part1.D10_PWM, J1.Vcc
  N2: Part1.D9_PWM, J1.pulse
  N3: Part1.D4_PWM, S2.L2
  N4: Part1.D51, J2.pulse
  N5: Part1.D52, J2.Vcc

notes:
  Ear LED
  Eye LED
  limit switch
